# Fritzing sketch Butonla_Led_Yakma_Devresi (saved by Fritzing 0.9.2b)
breadboards: 1

parts:
  S1 = Pushbutton [package="[THT]"]
  R1 = Resistor [tolerance=±5% resistance=330 package=THT]
  R2 = Resistor [tolerance=±5% resistance=10k package=THT]
  LED1 = LED - 5mm [color="Red (633nm)" package="5 mm [THT]"]
  Eleman1 = Arduino Uno (Rev3)

nets:
  N1: S1.Pin_1, S1.Pin_2, R2.Pin_1, Eleman1.D8
  N2: S1.Pin_3, S1.Pin_4
  N3: R1.Pin_0, LED1.anode
  N4: R1.Pin_1, Eleman1.D10_PWM/SS
  N5: R2.Pin_0, LED1.cathode
