# Fritzing sketch pot la (saved by Fritzing 0.9.2b)
breadboards: 1

parts:
  Eleman1 = Arduino Uno (Rev3)
  RE1 = Rotary Encoder [package=THT]

nets:
  N1: Eleman1.A0, RE1.EncoderPinC
  N2: Eleman1.5V, RE1.EncoderPinA
  N3: Eleman1.GND, RE1.EncoderPinB
