# Fritzing sketch fritzing_devresi (saved by Fritzing 0.9.2b)
breadboards: 1

parts:
  Eleman1 = Arduino Uno (Rev3)
  R1 = Resistor [tolerance=±5% resistance=330 package=THT]
  LED1 = LED - 5mm [color="Red (633nm)" package="5 mm [THT]"]

nets:
  N1: Eleman1.D2, R1.Pin_1
  N2: Eleman1.GND, LED1.cathode
  N3: R1.Pin_0, LED1.anode
